# Fritzing sketch esp8266-design (saved by Fritzing 0.9.3b)
breadboards: 1

parts:
  Part1 = Triple Axis Accelerometer Breakout - ADXL345
  Part2 = Adafruit HUZZAH32 ESP32 Feather [part_number="Adafruit #3405"]
  U1 = LIPO-1000mAh [package=lipo-1000]  # not connected

nets:
  GND: Part1.GND, Part2.GND
  VCC: Part1.VCC, Part2.3.3V
  N1: Part1.SDA, Part2.SDA
  N2: Part1.SCL, Part2.SCL
